# Fritzing sketch sketch (saved by Fritzing 0.9.3b)
breadboards: 1

parts:
  U1 = NodeMCU V1.0
  LED1 = smd LED [color="Red (633nm)" package="0603 [SMD]"]
  DS1 = DS18B20 1-Wire Temperature Sensor [part_number=DS18B20]
  R1 = Resistor [tolerance=±5% resistance=4.7k package=THT]

nets:
  N1: U1.D3, DS1.DQ, R1.Pin_1
  N2: U1.D4, LED1.anode
  3V3: U1.3V3, DS1.VDD, R1.Pin_0
  GND: U1.GND, LED1.cathode, DS1.GND

custom parts:
  NodeMCU V1.0: ESP8266 based NodeMCU
