# Fritzing sketch sketch32 (saved by Fritzing 0.9.3b)
breadboards: 1

parts:
  U1 = NodeMCU V1.0
  LED1 = smd LED [color="Red (633nm)" package="0603 [SMD]"]
  DS1 = DS18B20 1-Wire Temperature Sensor [part_number=DS18B20]
  R1 = Resistor [tolerance=±5% resistance=4.7k package=THT]
  R2 = Resistor [tolerance=±5% resistance=220 package=THT]

nets (from the breadboard view):
  N1: U1.3V3, DS1.DQ, R1.Pin_1
  GND: U1.GND, LED1.cathode, DS1.GND
  N2: U1.D6, R2.Pin_1
  N3: U1.A0, DS1.VDD, R1.Pin_0
  N4: LED1.anode, R2.Pin_0

custom parts:
  NodeMCU V1.0: ESP8266 based NodeMCU
